# Fritzing sketch sid-controller (saved by Fritzing 0.9.3b)
circuit board: 6cm x 4cm
circuit board: 2.72617cm x 2.1587cm
perfboards: 1

parts:
  IC1 = IC, DIP package, 28 pins [chip_label=6581SID]
  IC = IC, DIP package, 16 pins [chip_label=74LS174N]
  C1 = Ceramic Capacitor [capacitance=2.2nF package="100 mil [THT, multilayer]"]
  C2 = Ceramic Capacitor [capacitance=2.2nF package="100 mil [THT, multilayer]"]
  C3 = Ceramic Capacitor [capacitance=100nF package="100 mil [THT, multilayer]"]
  C4 = Ceramic Capacitor [capacitance=100nF voltage=16V package="100 mil [THT, multilayer]"]
  R1 = Resistor [tolerance=±5% resistance=1k package=THT]
  TRS1 = Audio Jack (TRS) 3.5mm [package="4Ucon 08780 [THT]"]
  C5 = Tantalum Capacitor [capacitance=4.7µF package="100 mil [THT, tantalum]"]
  J2 = screw terminal, 2 pins
  J2_2 = screw terminal, 2 pins
  J4 = male pin header, 3 pins [form="♂ (male)"]
  J3 = molex pin header, 11 pins [form=molex]
  C6 = Ceramic Capacitor [capacitance=100nF package="100 mil [THT, multilayer]"]

nets:
  N1: IC1.pin1, C1.0
  N2: IC1.pin2, C1.1
  N3: IC1.pin3, C2.0
  N4: IC1.pin4, C2.1
  N5: IC1.pin5, IC.pin15
  N6: IC1.pin6, J3.pin9
  N7: IC1.pin7, IC1.pin8, J3.pin10
  N8: IC1.pin9, IC.pin2
  N9: IC1.pin10, IC.pin5
  N10: IC1.pin11, IC.pin7
  N11: IC1.pin12, IC.pin10
  N12: IC1.pin13, IC.pin12
  GND: IC1.pin14, IC.pin8, C3.0, C4.0, J4.pin1, C6.0
  N13: IC1.pin15, IC.pin3, J3.pin8
  N14: IC1.pin16, IC.pin4, J3.pin7
  N15: IC1.pin17, IC.pin6, J3.pin6
  N16: IC1.pin18, IC.pin11, J3.pin5
  N17: IC1.pin19, IC.pin13, J3.pin4
  N18: IC1.pin20, IC.pin14, J3.pin3
  N19: IC1.pin21, J3.pin2
  N20: IC1.pin22, J3.pin1
  5V: IC1.pin25, IC.pin1, C3.1, J4.pin3
  12V: IC1.pin28, C4.1, J4.pin2
  N21: IC.pin9, J3.pin11
  N22: IC.pin16, C6.1
  N23: R1.Pin_0, J2.pin2, J2_2.pin2
  N24: R1.Pin_1, C5.+
  N25: TRS1.Sleeve, J2.pin1, J2_2.pin1
  N26: TRS1.Ring, TRS1.Tip, C5.-

notes:
  D39
  D41
  D43
  D45
  D47
  D49
  D51
  D53
  D37
  D35
  5V
  12V
  GND
  Audio IN
  D46
